// Logisim project final circuit.circ as structural Verilog: 4 circuits, main circuit main
module main (
  input  A0,
  input  B0,
  input  S0,
  input  S1,
  input  A1,
  input  B1,
  input  [3:0] A1_A0_B1_B0
);

  wire and_1_out, and_2_out, and_3_out, and_4_out, and_5_out, and_6_out, and_7_out, comparetor_1_a_b,
       comparetor_1_a_b_2, comparetor_1_a_b_3, or_1_out, or_2_out, xor_1_out, xor_2_out, xor_3_out,
       xor_4_out, xor_5_out, xor_6_out, xor_7_out, xor_8_out;

  and and_1 (and_1_out, S0, S1);
  comparetor comparetor_1 (
    .in_1(and_1_out), .A1_A0_B1_B0(A1_A0_B1_B0), .A_B(comparetor_1_a_b), .A_B_2(comparetor_1_a_b_2),
    .A_B_3(comparetor_1_a_b_3));
  xor xor_1 (xor_1_out, B0, S1);
  xor xor_2 (xor_2_out, S0, S1);
  xor xor_3 (xor_3_out, B1, S1);
  LED A_B (.in(comparetor_1_a_b));
  LED A_B_2 (.in(comparetor_1_a_b_2));
  and and_2 (and_2_out, A0, xor_2_out, xor_1_out);
  and and_3 (and_3_out, A1, xor_2_out, xor_3_out);
  LED A_B_3 (.in(comparetor_1_a_b_3));
  xor xor_4 (xor_4_out, A0, xor_1_out);
  xor xor_5 (xor_5_out, A1, xor_3_out);
  and and_4 (and_4_out, xor_4_out, xor_2_out, S1);
  and and_5 (and_5_out, xor_5_out, xor_2_out, or_1_out);
  xor xor_6 (xor_6_out, xor_4_out, S1);
  xor xor_7 (xor_7_out, xor_5_out, or_1_out);
  or or_1 (or_1_out, and_4_out, and_2_out);
  or or_2 (or_2_out, and_5_out, and_3_out);
  and and_6 (and_6_out, xor_6_out, xor_2_out);
  LED u_S0 (.in(and_6_out));
  and and_7 (and_7_out, xor_7_out, xor_2_out);
  LED u_S1 (.in(and_7_out));
  LED OV (.in(xor_8_out));
  xor xor_8 (xor_8_out, or_1_out, or_2_out);

  // Notes on the sheet:
  //   C0
  //   C1
  //   00 --> oFF
  //   01 --> ADDING
  //   10 --> SUBTRACTING
  //   11 --> COMPARETOR
endmodule

module comparetor (
  input  in_1,
  input  [3:0] A1_A0_B1_B0,
  output A_B,
  output A_B_2,
  output A_B_3
);

  wire decoder_1_out0, decoder_1_out1, decoder_1_out2, decoder_1_out3, decoder_1_out4, decoder_1_out5,
       decoder_1_out6, decoder_1_out7, decoder_1_out8, decoder_1_out9, decoder_1_out10, decoder_1_out11,
       decoder_1_out12, decoder_1_out13, decoder_1_out14, decoder_1_out15, not_1_out, not_2_out, not_3_out,
       not_4_out, not_5_out, not_6_out, not_7_out, not_8_out, not_9_out, not_10_out, not_11_out, not_12_out,
       not_13_out, not_14_out, not_15_out, not_16_out;

  not not_1 (not_1_out, decoder_1_out0);
  not not_2 (not_2_out, decoder_1_out2);
  not not_3 (not_3_out, decoder_1_out4);
  not not_4 (not_4_out, decoder_1_out6);
  not not_5 (not_5_out, decoder_1_out8);
  not not_6 (not_6_out, decoder_1_out10);
  not not_7 (not_7_out, decoder_1_out12);
  not not_8 (not_8_out, decoder_1_out14);
  Decoder #(.select(4), .disabled(0)) decoder_1 (
    .out0(decoder_1_out0), .out1(decoder_1_out1), .out2(decoder_1_out2), .out3(decoder_1_out3),
    .out4(decoder_1_out4), .out5(decoder_1_out5), .out6(decoder_1_out6), .out7(decoder_1_out7),
    .out8(decoder_1_out8), .out9(decoder_1_out9), .out10(decoder_1_out10), .out11(decoder_1_out11),
    .out12(decoder_1_out12), .out13(decoder_1_out13), .out14(decoder_1_out14), .out15(decoder_1_out15),
    .sel(A1_A0_B1_B0), .en(in_1));
  not not_9 (not_9_out, decoder_1_out1);
  not not_10 (not_10_out, decoder_1_out3);
  not not_11 (not_11_out, decoder_1_out5);
  not not_12 (not_12_out, decoder_1_out7);
  not not_13 (not_13_out, decoder_1_out9);
  not not_14 (not_14_out, decoder_1_out11);
  not not_15 (not_15_out, decoder_1_out13);
  not not_16 (not_16_out, decoder_1_out15);
  nand nand_1 (A_B_3, not_9_out, not_2_out, not_4_out, not_10_out, not_8_out);
  nand nand_2 (A_B, not_1_out, not_11_out, not_12_out, not_6_out, not_15_out, not_16_out);
  nand nand_3 (A_B_2, not_3_out, not_5_out, not_13_out, not_14_out, not_7_out);
endmodule

module h (
  input  A,
  input  B,
  output out_3
);

  wire not_1_out, xor_1_out, xor_2_out;

  xor xor_1 (xor_1_out, B, not_1_out);
  not not_1 (not_1_out, 1'b1);
  xor xor_2 (xor_2_out, A, xor_1_out);
  xor xor_3 (out_3, xor_2_out, not_1_out, not_1_out);
endmodule

module final_project (
  input  A0,
  input  B0,
  input  S0,
  input  S1,
  input  A1,
  input  B1,
  input  [3:0] A1_A0_B1_B0
);

  wire and_1_out, and_2_out, and_3_out, and_4_out, and_5_out, and_6_out, and_7_out, comparetor_1_a_b,
       comparetor_1_a_b_2, comparetor_1_a_b_3, or_1_out, or_2_out, xor_1_out, xor_2_out, xor_3_out,
       xor_4_out, xor_5_out, xor_6_out, xor_7_out, xor_8_out;

  and and_1 (and_1_out, S0, S1);
  xor xor_1 (xor_1_out, S0, S1);
  xor xor_2 (xor_2_out, B0, S1);
  xor xor_3 (xor_3_out, B1, S1);
  comparetor comparetor_1 (
    .in_1(and_1_out), .A1_A0_B1_B0(A1_A0_B1_B0), .A_B(comparetor_1_a_b), .A_B_2(comparetor_1_a_b_2),
    .A_B_3(comparetor_1_a_b_3));
  LED A_B (.in(comparetor_1_a_b));
  LED A_B_2 (.in(comparetor_1_a_b_2));
  and and_2 (and_2_out, xor_2_out, xor_1_out, A0);
  and and_3 (and_3_out, xor_3_out, xor_1_out, A1);
  LED A_B_3 (.in(comparetor_1_a_b_3));
  xor xor_4 (xor_4_out, A0, xor_2_out);
  xor xor_5 (xor_5_out, A1, xor_3_out);
  xor xor_6 (xor_6_out, xor_4_out, S1);
  and and_4 (and_4_out, S1, xor_4_out, xor_1_out);
  xor xor_7 (xor_7_out, xor_5_out, or_1_out);
  and and_5 (and_5_out, or_1_out, xor_5_out, xor_1_out);
  and and_6 (and_6_out, xor_6_out, xor_1_out);
  or or_1 (or_1_out, and_4_out, and_2_out);
  and and_7 (and_7_out, xor_7_out, xor_1_out);
  LED u_S1 (.in(and_7_out));
  or or_2 (or_2_out, and_5_out, and_3_out);
  LED u_S0 (.in(and_6_out));
  xor xor_8 (xor_8_out, or_1_out, or_2_out);
  LED OV (.in(xor_8_out));

  // Notes on the sheet:
  //   00 --> oFF
  //   01 --> ADDING
  //   S1 ---> MSB
  //   10 --> SUBTRACTING
  //   11 --> COMPARETOR
  //   C0
  //   C1
endmodule
